// Logisim project barrera_codigo(1).circ as structural Verilog: 9 circuits, main circuit top
module M1_registro_estado (
  input  D1,
  input  D0,
  input  CLK,
  input  RST,
  output out_5,
  output out_6
);

  D_Flip_Flop Q1 (.D(D1), .clk(CLK), .Q(out_5), .reset(RST));  // open: Qn, preset
  D_Flip_Flop Q0 (.D(D0), .clk(CLK), .Q(out_6), .reset(RST));  // open: Qn, preset

  // Notes on the sheet:
  //   FSM 1 (Moore) - State register (2 FF D, reset asincrono)
  //   Guarda el estado Q1 Q0.  RST = 1 lo lleva a 00 (CERRADA) sin esperar el flanco.
endmodule

module M1_next_state_logic (
  input  SENSOR,
  input  OK,
  input  Q1,
  input  Q0,
  output D1,
  output D0
);

  wire and_1_out, and_2_out, and_3_out, and_4_out, and_5_out, not_1_out, not_2_out, not_3_out;

  not not_1 (not_1_out, SENSOR);
  not not_2 (not_2_out, Q1);
  not not_3 (not_3_out, Q0);
  and and_1 (and_1_out, not_2_out, Q0);
  and and_2 (and_2_out, Q1, not_3_out);
  and and_3 (and_3_out, Q1, Q0, SENSOR);
  and and_4 (and_4_out, not_2_out, not_3_out, OK);
  and and_5 (and_5_out, Q1, not_3_out, not_1_out);
  or or_1 (D1, and_1_out, and_2_out, and_3_out);
  or or_2 (D0, and_4_out, and_5_out);

  // Notes on the sheet:
  //   FSM 1 (Moore) - Next state logic
  //   D1 D0 = estado siguiente = f(estado actual Q1 Q0, SENSOR, OK del verificador de codigo)
  //   D1 = Q1'Q0 + Q1Q0' + Q1Q0.SENSOR
  //   D0 = Q1'Q0'.OK + Q1Q0'.SENSOR'
  //   Un termino AND por cada flecha del diagrama de estados.
  //   SENSOR
  //   SENSOR'
  //   OK
  //   Q1
  //   Q1'
  //   Q0
  //   Q0'
endmodule

module M1_output_logic (
  input  Q1,
  input  Q0,
  output CERRADA,
  output ABRIENDO,
  output ABIERTA,
  output CERRANDO
);

  wire not_1_out, not_2_out;

  not not_1 (not_1_out, Q1);
  not not_2 (not_2_out, Q0);
  and and_1 (CERRADA, not_1_out, not_2_out);
  and and_2 (ABRIENDO, not_1_out, Q0);
  and and_3 (ABIERTA, Q1, not_2_out);
  and and_4 (CERRANDO, Q1, Q0);

  // Notes on the sheet:
  //   FSM 1 (Moore) - Output logic
  //   Salidas = f(estado actual)
  //   CERRADA = Q1'Q0'   ABRIENDO = Q1'Q0   ABIERTA = Q1Q0'   CERRANDO = Q1Q0
  //   Moore: las salidas dependen SOLO del estado (un LED por estado).
  //   Q1
  //   Q1'
  //   Q0
  //   Q0'
endmodule

module M1_FSM_Moore (
  input  CLK,
  input  RST,
  input  SENSOR,
  input  OK,
  output CERRADA,
  output ABRIENDO,
  output ABIERTA,
  output CERRANDO,
  output Q1,
  output Q0
);

  wire m1_next_state_logic_1_d0, m1_next_state_logic_1_d1;

  M1_next_state_logic m1_next_state_logic_1 (
    .SENSOR(SENSOR), .OK(OK), .Q1(Q1), .Q0(Q0), .D1(m1_next_state_logic_1_d1), .D0(m1_next_state_logic_1_d0));
  M1_registro_estado m1_registro_estado_1 (
    .D1(m1_next_state_logic_1_d1), .D0(m1_next_state_logic_1_d0), .CLK(CLK), .RST(RST), .out_5(Q1), .out_6(Q0));
  M1_output_logic m1_output_logic_1 (
    .Q1(Q1), .Q0(Q0), .CERRADA(CERRADA), .ABRIENDO(ABRIENDO), .ABIERTA(ABIERTA), .CERRANDO(CERRANDO));

  // Notes on the sheet:
  //   FSM 1 (Moore) - Controlador de la barrera
  //   Next state logic -> State register (Q1 Q0) -> Output logic.  Q realimenta a la Next state logic.
  //   Q1 Q0 (estado actual) realimentan a la Next state logic
  //   Next state logic
  //   State register
  //   Output logic
endmodule

module M2_registro_estado (
  input  D1,
  input  D0,
  input  CLK,
  output out_4,
  output out_5
);

  D_Flip_Flop P1 (.D(D1), .clk(CLK), .Q(out_4));  // open: Qn, preset, reset
  D_Flip_Flop P0 (.D(D0), .clk(CLK), .Q(out_5));  // open: Qn, preset, reset

  // Notes on the sheet:
  //   FSM 2 (Mealy) - State register (2 FF D)
  //   P1 P0 = cuantas teclas del codigo van bien:  00 ninguna,  01 va la 1a (A),  10 van 2 (A, C).  (Reset sincronico en la next state logic.)
endmodule

module M2_next_state_logic (
  input  A,
  input  B,
  input  C,
  input  EN,
  input  RST,
  input  P1,
  input  P0,
  output D1,
  output D0
);

  wire and_1_out, and_2_out, and_3_out, and_4_out, not_1_out, not_2_out, not_3_out, not_4_out, not_5_out,
       not_6_out;

  not not_1 (not_1_out, A);
  not not_2 (not_2_out, B);
  not not_3 (not_3_out, C);
  not not_4 (not_4_out, RST);
  not not_5 (not_5_out, P1);
  not not_6 (not_6_out, P0);
  and and_1 (and_1_out, not_4_out, EN, not_5_out, P0, C);
  and and_2 (and_2_out, not_4_out, EN, P1, not_6_out, not_1_out, not_2_out);
  and and_3 (and_3_out, not_4_out, EN, not_5_out, not_6_out, A);
  and and_4 (and_4_out, not_4_out, EN, not_5_out, P0, not_2_out, not_3_out);
  or or_1 (D1, and_1_out, and_2_out);
  or or_2 (D0, and_3_out, and_4_out);

  // Notes on the sheet:
  //   FSM 2 (Mealy) - Next state logic
  //   D1 D0 = estado siguiente = f(P1 P0, teclas A B C, EN, RST)   (se pulsa una tecla a la vez)
  //   D1 = RST'.EN.P1'.P0.C + RST'.EN.P1.P0'.A'.B'
  //   D0 = RST'.EN.P1'.P0'.A + RST'.EN.P1'.P0.B'.C'
  //   Codigo secreto A -> C -> B: la tecla correcta avanza, mantenerla no cambia nada, una equivocada regresa a 00.
  //   EN = 0 (barrera no cerrada) o RST = 1: vuelve a 00.
  //   A
  //   A'
  //   B
  //   B'
  //   C
  //   C'
  //   EN
  //   RST
  //   RST'
  //   P1
  //   P1'
  //   P0
  //   P0'
endmodule

module M2_output_logic (
  input  A,
  input  B,
  input  C,
  input  EN,
  input  P1,
  input  P0,
  output CODIGO_OK,
  output ALARMA,
  output PASO_1,
  output PASO_2
);

  wire and_2_out, and_3_out, and_4_out, and_5_out, not_1_out, not_2_out, not_3_out, not_4_out;

  not not_1 (not_1_out, A);
  not not_2 (not_2_out, C);
  not not_3 (not_3_out, P1);
  not not_4 (not_4_out, P0);
  and and_1 (CODIGO_OK, EN, P1, not_4_out, B, not_1_out, not_2_out);
  and and_2 (and_2_out, EN, not_3_out, not_4_out, B);
  and and_3 (and_3_out, EN, not_3_out, not_4_out, C);
  and and_4 (and_4_out, EN, not_3_out, P0, B);
  and and_5 (and_5_out, EN, P1, not_4_out, A);
  and and_6 (PASO_1, not_3_out, P0);
  and and_7 (PASO_2, P1, not_4_out);
  or or_1 (ALARMA, and_2_out, and_3_out, and_4_out, and_5_out);

  // Notes on the sheet:
  //   FSM 2 (Mealy) - Output logic
  //   Salidas = f(estado P1 P0, teclas A B C, EN)
  //   CODIGO_OK = EN.P1.P0'.B.A'.C'   (van A y C bien y ahora B)
  //   ALARMA = EN.(P1'P0'.B + P1'P0'.C + P1'P0.B + P1P0'.A)   (tecla equivocada en cada paso)
  //   PASO_1 = P1'P0   PASO_2 = P1P0'
  //   Mealy: CODIGO_OK y ALARMA cambian en cuanto pulsas la tecla (dependen de las teclas Y del estado).
  //   A
  //   A'
  //   B
  //   C
  //   C'
  //   EN
  //   P1
  //   P1'
  //   P0
  //   P0'
endmodule

module M2_FSM_Mealy (
  input  A,
  input  B,
  input  C,
  input  EN,
  input  RST,
  input  CLK,
  output CODIGO_OK,
  output ALARMA,
  output PASO_1,
  output PASO_2
);

  wire m2_next_state_logic_1_d0, m2_next_state_logic_1_d1, m2_registro_estado_1_out_4,
       m2_registro_estado_1_out_5;

  M2_next_state_logic m2_next_state_logic_1 (
    .A(A), .B(B), .C(C), .EN(EN), .RST(RST), .P1(m2_registro_estado_1_out_4),
    .P0(m2_registro_estado_1_out_5), .D1(m2_next_state_logic_1_d1), .D0(m2_next_state_logic_1_d0));
  M2_registro_estado m2_registro_estado_1 (
    .D1(m2_next_state_logic_1_d1), .D0(m2_next_state_logic_1_d0), .CLK(CLK),
    .out_4(m2_registro_estado_1_out_4), .out_5(m2_registro_estado_1_out_5));
  M2_output_logic m2_output_logic_1 (
    .A(A), .B(B), .C(C), .EN(EN), .P1(m2_registro_estado_1_out_4), .P0(m2_registro_estado_1_out_5),
    .CODIGO_OK(CODIGO_OK), .ALARMA(ALARMA), .PASO_1(PASO_1), .PASO_2(PASO_2));

  // Notes on the sheet:
  //   FSM 2 (Mealy) - Verificador del codigo secreto (A, luego C, luego B)
  //   Mealy: las teclas y EN llegan a la Next state logic Y a la Output logic; las salidas reaccionan sin esperar el reloj.
  //   P1 P0 (estado actual) realimentan a la Next state logic
  //   Next state logic
  //   State register
  //   Output logic
endmodule

module top (
  input  RST,
  input  SENSOR,
  output Q1,
  output Q0
);

  wire A_out, B_out, C_out, CLK_out, m1_fsm_moore_1_abierta, m1_fsm_moore_1_abriendo, m1_fsm_moore_1_cerrada,
       m1_fsm_moore_1_cerrando, m2_fsm_mealy_1_alarma, m2_fsm_mealy_1_codigo_ok, m2_fsm_mealy_1_paso_1,
       m2_fsm_mealy_1_paso_2;

  Clock CLK (.out(CLK_out));
  Button A (.out(A_out));
  Button B (.out(B_out));
  Button C (.out(C_out));
  M1_FSM_Moore m1_fsm_moore_1 (
    .CLK(CLK_out), .RST(RST), .SENSOR(SENSOR), .OK(m2_fsm_mealy_1_codigo_ok),
    .CERRADA(m1_fsm_moore_1_cerrada), .ABRIENDO(m1_fsm_moore_1_abriendo), .ABIERTA(m1_fsm_moore_1_abierta),
    .CERRANDO(m1_fsm_moore_1_cerrando), .Q1(Q1), .Q0(Q0));
  M2_FSM_Mealy m2_fsm_mealy_1 (
    .A(A_out), .B(B_out), .C(C_out), .EN(m1_fsm_moore_1_cerrada), .RST(RST), .CLK(CLK_out),
    .CODIGO_OK(m2_fsm_mealy_1_codigo_ok), .ALARMA(m2_fsm_mealy_1_alarma), .PASO_1(m2_fsm_mealy_1_paso_1),
    .PASO_2(m2_fsm_mealy_1_paso_2));
  LED CERRADA (.in(m1_fsm_moore_1_cerrada));
  LED ABRIENDO (.in(m1_fsm_moore_1_abriendo));
  LED ABIERTA (.in(m1_fsm_moore_1_abierta));
  LED CERRANDO (.in(m1_fsm_moore_1_cerrando));
  LED CODIGO_OK (.in(m2_fsm_mealy_1_codigo_ok));
  LED ALARMA (.in(m2_fsm_mealy_1_alarma));
  LED PASO_1 (.in(m2_fsm_mealy_1_paso_1));
  LED PASO_2 (.in(m2_fsm_mealy_1_paso_2));

  // Notes on the sheet:
  //   Barrera de estacionamiento con código secreto: dos FSM que interactúan
  //   FSM 2 (Mealy) verifica el código secreto A, C, B.   FSM 1 (Moore) mueve la barrera.   Un solo CLK y un solo RST.
  //   Cómo probarlo
  //   0) Simulate > Ticks Enabled (Ctrl+K).  Para ir paso a paso: desactívalo y haz clic sobre CLK.
  //   1) RST = 1 un momento y luego 0.  Se enciende CERRADA (rojo).
  //   2) CÓDIGO SECRETO = A, luego C, luego B.  Mantén pulsada cada tecla hasta que el LED de progreso
  //      se encienda y suéltala:  A -> PASO_1 (azul),  C -> PASO_2 (violeta),  B -> CODIGO_OK (cian, al instante,
  //      Mealy) y la barrera hace ABRIENDO (amarillo) -> ABIERTA (verde).
  //   3) Con SENSOR = 1 (hay un carro debajo) la barrera se queda ABIERTA.  Con SENSOR = 0 pasa a CERRANDO
  //      (naranja) -> CERRADA.  Si pones SENSOR = 1 mientras cierra, vuelve a ABIERTA (seguridad).
  //   4) CÓDIGO INCORRECTO: pulsa una tecla equivocada (p. ej. B primero, o A luego B) y se enciende
  //      ALARMA (morado); el progreso se borra y hay que empezar de nuevo.
  //   ENTRADAS (clic)
  //   SENSOR = hay un carro bajo la barrera
  //   TECLADO A B C (mantén el clic)
  //   FSM 1 -> FSM 2: CERRADA (EN: solo acepta código con la barrera cerrada)      FSM 2 -> FSM 1: CODIGO_OK (OK: abre la barrera)
  //   FSM 1 (Moore): estado de la barrera
  //   FSM 2 (Mealy): verificador de código
endmodule
